# Fritzing sketch blink (saved by Fritzing 0.3.19b)

parts:
  LED1 = yellow LED - 5mm
  R1 = Resistor [resistance=220 package=THT]
  IC1 = IC, DIP package, 8 pins [chip_label=08m spacing=300mil]
  VCC1 = obsolete Battery
  R2 = Resistor [resistance=220 package=THT]
  R3 = Resistor [resistance=22k package=THT]
  U1 = mystery part, 3 pins [chip_label="Serial Port Adapter" spacing=300mil]
  C1 = Ceramic Capacitor [package=THT]

nets:
  N1: LED1.cathode, IC1.pin8, VCC1.-, R2.Pin_1, U1.pin1, C1.pin_1
  N2: LED1.anode, R1.Pin_1
  N3: R1.Pin_0, IC1.pin6
  N4: IC1.pin1, VCC1.+, C1.pin_0
  N5: IC1.pin2, R3.Pin_1
  N6: IC1.pin7, U1.pin2
  N7: R2.Pin_0, R3.Pin_0, U1.pin3

notes:
  Actually 3 AA batteries
  Serial adapter
