# Fritzing sketch eyes (saved by Fritzing 0.4.3b)

parts:
  IC1 = IC, DIP package, 8 pins [chip_label=08m spacing=300mil]
  R2 = Resistor [resistance=10k package=THT]
  R3 = Resistor [resistance=22k package=THT]
  C1 = Ceramic Capacitor [package=THT]
  VCC1 = obsolete Battery
  R4 = Resistor [resistance=100 package=THT]
  R5 = Resistor [resistance=100 package=THT]
  R6 = Resistor [resistance=100 package=THT]
  LED1 = Red LED - 5mm
  LED2 = Red LED - 5mm
  LED3 = Red LED - 5mm
  LED4 = Red LED - 5mm
  LED5 = Red LED - 5mm
  LED6 = Red LED - 5mm

nets:
  N1: IC1.pin1, C1.pin_0, VCC1.+
  N2: IC1.pin2, R3.Pin_1
  N3: IC1.pin3, R6.Pin_0
  N4: IC1.pin5, R5.Pin_0
  N5: IC1.pin6, R4.Pin_0
  N6: IC1.pin8, R2.Pin_1, C1.pin_1, VCC1.-, LED2.cathode, LED4.cathode, LED6.cathode
  N7: R2.Pin_0, R3.Pin_0
  N8: R4.Pin_1, LED1.anode
  N9: R5.Pin_1, LED3.anode
  N10: R6.Pin_1, LED5.anode
  N11: LED1.cathode, LED2.anode
  N12: LED3.cathode, LED4.anode
  N13: LED5.cathode, LED6.anode

notes:
  Actually 3 AA batteries
